# Fritzing sketch EnvSight (saved by Fritzing 0.9.3b)
circuit board: 4.27462cm x 5.60627cm
breadboards: 1

parts:
  WeMos_D1_Mini1 = WeMos D1 Mini
  MQ-135 = MQ-3 breakout
  DHT22/DHT11 = Humidity and Temperature Sensor RHT03

nets:
  VCC: WeMos_D1_Mini1.5V, MQ-135.VCC, DHT22/DHT11.Vcc
  N1: WeMos_D1_Mini1.A0, MQ-135.AO
  N2: WeMos_D1_Mini1.D1, DHT22/DHT11.Data-signal
  N3: WeMos_D1_Mini1.G, MQ-135.GND, DHT22/DHT11.GND_2

notes:
  We-Mos D1 Mini/ ESP32
  DHT22

custom parts:
  MQ-3 breakout: Alcohol sensor is capable of detecting alcohol (ethanol) particles on itself and gives the information in digital form back to us to manipulate with it. SKU:101251 • Voltage: 5V DC • Power: max 750mW • Measurement range: 0.04-4mg/L
